// Logisim project pres.circ as structural Verilog: 16 circuits, main circuit 2.D flip flop
module _1_Logic_Gates (
  input  in_1,
  input  in_2,
  input  in_3,
  input  in_4,
  input  in_5,
  input  in_6,
  input  in_7,
  input  [3:0] _4_bit_wire,
  output out_9,
  output out_10,
  output out_11,
  output out_12,
  output Splitter,
  output [2:0] out_14
);

  and and_1 (out_9, in_1, in_2);
  not not_1 (out_10, in_3);
  or or_1 (out_11, in_4, in_5);
  nand nand_1 (out_12, in_6, in_7);

  assign out_14 = _4_bit_wire[3:1];
  assign Splitter = _4_bit_wire[0];

  // Notes on the sheet:
  //   AND
  //   NOT
  //   OR
  //   NAND
endmodule

module _2_D_flip_flop (
  input  Data,
  input  GateKeeper,
  input  Data_2,
  input  Gatekeeper_2,
  input  in_5,
  input  Data_3,
  output Q,
  output out_8,
  output Q_2
);

  wire nand_1_out, nand_2_out, nand_3_out, nand_4_out, nand_5_out, nand_6_out, nand_8_out, nand_9_out,
       nand_10_out, nand_12_out, not_1_out, not_2_out, not_3_out;

  not not_1 (not_1_out, Data);
  not not_2 (not_2_out, Gatekeeper_2);
  nand nand_1 (nand_1_out, Data, GateKeeper);
  nand nand_2 (nand_2_out, not_1_out, GateKeeper);
  nand nand_3 (nand_3_out, Data_2, not_2_out);
  nand nand_4 (nand_4_out, nand_3_out, not_2_out);
  not not_3 (not_3_out, not_2_out);
  nand nand_5 (nand_5_out, nand_3_out, nand_6_out);
  nand nand_6 (nand_6_out, nand_5_out, nand_4_out);
  nand nand_7 (Q, nand_1_out, nand_8_out);
  nand nand_8 (nand_8_out, Q, nand_2_out);
  D_Flip_Flop d_ff_1 (.clk(in_5), .D(Data_3), .Q(Q_2), .en(1'b1));  // open: Qn, preset, reset
  nand nand_9 (nand_9_out, nand_5_out, not_3_out);
  nand nand_10 (nand_10_out, nand_9_out, not_3_out);
  nand nand_11 (out_8, nand_9_out, nand_12_out);
  nand nand_12 (nand_12_out, out_8, nand_10_out);

  // Notes on the sheet:
  //   1:pass through
  //   0:remember value
  //   Remembers on the rising edge
  //   Gatekeeper / Clock
  //   There's also an enable.
  //   Flipflop ignores everything if 0
  //   Master-Slave D flip-flop
endmodule

module _3_Register (
  input  in_1,
  input  in_2,
  input  in_3,
  input  in_4,
  input  in_5,
  input  in_6,
  input  in_7,
  input  in_8,
  input  in_9,
  output out_10,
  output out_11,
  output out_12,
  output out_13,
  output out_14,
  output out_15,
  output out_16,
  output out_17
);

  wire button_1_out;

  Button button_1 (.out(button_1_out));
  D_Flip_Flop d_ff_1 (.clk(in_1), .D(in_2), .Q(out_10));  // open: Qn, preset, en, reset
  D_Flip_Flop d_ff_2 (.clk(in_1), .D(in_3), .Q(out_11));  // open: Qn, preset, en, reset
  D_Flip_Flop d_ff_3 (.clk(in_1), .D(in_4), .Q(out_12));  // open: Qn, preset, en, reset
  D_Flip_Flop d_ff_4 (.clk(in_1), .D(in_5), .Q(out_13));  // open: Qn, preset, en, reset
  Register #(.width(4)) register_1 (
    .D({in_9, in_8, in_7, in_6}), .Q({out_17, out_16, out_15, out_14}), .clk(button_1_out));  // open: en, clr
endmodule

module _4__Multiplexer (
  input  Inputs,
  input  in_2,
  input  Selector,
  input  in_4,
  input  in_5,
  input  in_6,
  input  in_7,
  input  in_8,
  input  in_9,
  output out_10,
  output out_11,
  output out_12
);

  wire and_1_out, and_2_out, multiplexer_2_out, multiplexer_3_out, not_1_out;

  not not_1 (not_1_out, Selector);
  Multiplexer multiplexer_1 (.in0(Inputs), .in1(in_2), .out(out_11), .sel(Selector));  // open: en
  and and_1 (and_1_out, Inputs, not_1_out);
  and and_2 (and_2_out, in_2, Selector);
  Multiplexer multiplexer_2 (.in0(in_6), .in1(in_7), .out(multiplexer_2_out), .sel(in_4));  // open: en
  Multiplexer multiplexer_3 (.in0(in_8), .in1(in_9), .out(multiplexer_3_out), .sel(in_4));  // open: en
  or or_1 (out_10, and_1_out, and_2_out);
  Multiplexer multiplexer_4 (.in0(multiplexer_2_out), .in1(multiplexer_3_out), .out(out_12), .sel(in_5));  // open: en
endmodule

module _5__ALU (
  input  [7:0] in_1,
  input  [1:0] in_2,
  input  [7:0] in_3,
  output [7:0] out_4
);

  wire [7:0] adder_1_out, negator_1_out, subtractor_1_out;

  Adder adder_1 (.a(in_1), .b(in_3), .out(adder_1_out));  // open: cin, cout
  Subtractor subtractor_1 (.a(in_1), .b(in_3), .out(subtractor_1_out));  // open: bin, bout
  Negator negator_1 (.in(in_1), .out(negator_1_out));
  Multiplexer #(.select(2), .width(8)) multiplexer_1 (
    .in0(adder_1_out), .in1(subtractor_1_out), .in2(negator_1_out), .in3(in_1), .out(out_4), .sel(in_2));  // open: en

  // Notes on the sheet:
  //   Arithmetic logic unit
endmodule

module _6__Decoder (
  input  in_1,
  input  in_2,
  output _0,
  output _1,
  output _2,
  output _3,
  output out_7,
  output out_8,
  output out_9,
  output out_10
);

  wire not_1_out, not_2_out, not_3_out, not_4_out;

  not not_1 (not_1_out, in_1);
  not not_2 (not_2_out, in_2);
  not not_3 (not_3_out, in_1);
  not not_4 (not_4_out, in_2);
  Decoder #(.select(2)) decoder_1 (
    .out0(out_7), .out1(out_8), .out2(out_9), .out3(out_10), .sel({in_1, in_2}));  // open: en
  and and_1 (_0, not_1_out, not_2_out);
  and and_2 (_1, not_3_out, in_2);
  and and_3 (_2, in_1, not_4_out);
  and and_4 (_3, in_1, in_2);
endmodule

module _7__CPU_A (
  input  [1:0] in_1,
  input  [7:0] in_2,
  input  [1:0] Reg_A,
  input  [1:0] Reg_B,
  input  [1:0] Which_function,
  output [7:0] out_6
);

  wire button_1_out, decoder_1_out0, decoder_1_out1, decoder_1_out2, decoder_1_out3;
  wire [7:0] multiplexer_1_out, multiplexer_2_out, register_1_q, register_2_q, register_3_q, register_4_q;

  Decoder #(.select(2), .enable("false")) decoder_1 (
    .out0(decoder_1_out0), .out1(decoder_1_out1), .out2(decoder_1_out2), .out3(decoder_1_out3), .sel(in_1));
  Button button_1 (.out(button_1_out));
  Register register_1 (.D(in_2), .en(decoder_1_out0), .Q(register_1_q), .clk(button_1_out));  // open: clr
  Register register_2 (.D(in_2), .en(decoder_1_out1), .Q(register_2_q), .clk(button_1_out));  // open: clr
  Register register_3 (.D(in_2), .en(decoder_1_out2), .Q(register_3_q), .clk(button_1_out));  // open: clr
  Register register_4 (.D(in_2), .en(decoder_1_out3), .Q(register_4_q), .clk(button_1_out));  // open: clr
  Multiplexer #(.select(2), .width(8), .enable("false")) multiplexer_1 (
    .in0(register_1_q), .in1(register_2_q), .in2(register_3_q), .in3(register_4_q), .out(multiplexer_1_out),
    .sel(Reg_A));
  Multiplexer #(.select(2), .width(8), .enable("false")) multiplexer_2 (
    .in0(register_1_q), .in1(register_2_q), .in2(register_3_q), .in3(register_4_q), .out(multiplexer_2_out),
    .sel(Reg_B));
  _5__ALU u_5_alu_1 (.in_1(multiplexer_1_out), .in_2(Which_function), .in_3(multiplexer_2_out), .out_4(out_6));

  // Notes on the sheet:
  //   Which register to load
  //   What value to load
  //   Clock signal
  //   Loading registers and then doing math with their contents
  //   0: plus
  //   1: minus
  //   2: negate
  //   3: pass through
endmodule

module _8__CPB_B (
  input  [1:0] Reg_A,
  input  [1:0] Reg_B,
  input  [1:0] Which_function,
  input  in_4,
  input  [1:0] in_5,
  input  [7:0] in_6,
  output [7:0] Output
);

  wire button_1_out, decoder_1_out0, decoder_1_out1, decoder_1_out2, decoder_1_out3;
  wire [7:0] multiplexer_1_out, multiplexer_2_out, multiplexer_3_out, register_1_q, register_2_q,
       register_3_q, register_4_q;

  Decoder #(.select(2), .enable("false")) decoder_1 (
    .out0(decoder_1_out0), .out1(decoder_1_out1), .out2(decoder_1_out2), .out3(decoder_1_out3), .sel(in_5));
  Multiplexer #(.width(8), .enable("false")) multiplexer_1 (
    .in0(in_6), .in1(Output), .out(multiplexer_1_out), .sel(in_4));
  Button button_1 (.out(button_1_out));
  Register register_1 (.D(multiplexer_1_out), .en(decoder_1_out0), .Q(register_1_q), .clk(button_1_out));  // open: clr
  Register register_2 (.D(multiplexer_1_out), .en(decoder_1_out1), .Q(register_2_q), .clk(button_1_out));  // open: clr
  Register register_3 (.D(multiplexer_1_out), .en(decoder_1_out2), .Q(register_3_q), .clk(button_1_out));  // open: clr
  Register register_4 (.D(multiplexer_1_out), .en(decoder_1_out3), .Q(register_4_q), .clk(button_1_out));  // open: clr
  Multiplexer #(.select(2), .width(8), .enable("false")) multiplexer_2 (
    .in0(register_1_q), .in1(register_2_q), .in2(register_3_q), .in3(register_4_q), .out(multiplexer_2_out),
    .sel(Reg_A));
  Multiplexer #(.select(2), .width(8), .enable("false")) multiplexer_3 (
    .in0(register_1_q), .in1(register_2_q), .in2(register_3_q), .in3(register_4_q), .out(multiplexer_3_out),
    .sel(Reg_B));
  _5__ALU u_5_alu_1 (.in_1(multiplexer_2_out), .in_2(Which_function), .in_3(multiplexer_3_out), .out_4(Output));

  // Notes on the sheet:
  //   Load from ALU or literal
  //   Which register to load
  //   Clock signal
  //   What value to load
  //   Putting the math results back into the registers
  //   0: Add
  //   1: Sub
  //   2: Negate
  //   3: Pass through
endmodule

module _9__RAM (
  output [3:0] out_1,
  output [3:0] out_2
);

  wire button_1_out;

  Button button_1 (.out(button_1_out));
  Counter #(.width(4), .max('hf)) counter_1 (
    .count(button_1_out), .Q(out_2), .clk(button_1_out));  // open: load, D, carry, clr
  RAM #(.addrWidth(4), .dataWidth(4)) ram_1 (.addr(out_2), .data(out_1));  // open: sel, clk, ld, clr
endmodule

module _10__CPU_C (
  output [7:0] Output
);

  wire button_1_out, button_2_out, button_3_out, decoder_1_out0, decoder_1_out1, decoder_1_out2,
       decoder_1_out3;
  wire [7:0] counter_1_q, multiplexer_1_out, multiplexer_2_out, multiplexer_3_out, ram_1_data_2,
       register_1_q, register_2_q, register_3_q, register_4_q;
  wire [16:0] ram_1_data;

  Counter counter_1 (
    .count(button_2_out), .Q(counter_1_q), .clk(button_2_out), .clr(button_1_out));  // open: load, D, carry
  Button button_1 (.out(button_1_out));
  Decoder #(.select(2), .enable("false")) decoder_1 (
    .out0(decoder_1_out0), .out1(decoder_1_out1), .out2(decoder_1_out2), .out3(decoder_1_out3),
    .sel(ram_1_data[2:1]));
  Button button_2 (.out(button_2_out));
  Multiplexer #(.width(8), .enable("false")) multiplexer_1 (
    .in0(ram_1_data_2), .in1(Output), .out(multiplexer_1_out), .sel(ram_1_data[0]));
  RAM #(.dataWidth(17)) ram_1 (
    .addr(counter_1_q), .data({ram_1_data[16:11], ram_1_data_2, ram_1_data[2:0]}));  // open: sel, clk, ld, clr
  Register register_1 (
    .D(multiplexer_1_out), .en(decoder_1_out0), .Q(register_1_q), .clk(button_2_out), .clr(button_3_out));
  Register register_2 (
    .D(multiplexer_1_out), .en(decoder_1_out1), .Q(register_2_q), .clk(button_2_out), .clr(button_3_out));
  Register register_3 (
    .D(multiplexer_1_out), .en(decoder_1_out2), .Q(register_3_q), .clk(button_2_out), .clr(button_3_out));
  Register register_4 (
    .D(multiplexer_1_out), .en(decoder_1_out3), .Q(register_4_q), .clk(button_2_out), .clr(button_3_out));
  Button button_3 (.out(button_3_out));
  Multiplexer #(.select(2), .width(8), .enable("false")) multiplexer_2 (
    .in0(register_1_q), .in1(register_2_q), .in2(register_3_q), .in3(register_4_q), .out(multiplexer_2_out),
    .sel(ram_1_data[12:11]));
  Multiplexer #(.select(2), .width(8), .enable("false")) multiplexer_3 (
    .in0(register_1_q), .in1(register_2_q), .in2(register_3_q), .in3(register_4_q), .out(multiplexer_3_out),
    .sel(ram_1_data[14:13]));
  _5__ALU u_5_alu_1 (.in_1(multiplexer_2_out), .in_2(ram_1_data[16:15]), .in_3(multiplexer_3_out), .out_4(Output));

  // Notes on the sheet:
  //   Which register to load
  //   Program
  //   Counter
  //   Reset
  //   Clock signal
  //   <---
  //   Reset
  //   Load from literal
  //   or ALU result
  //   What literal to load
  //   Instead of many pins, lets use RAM
  //   Reg A
  //   Reg B
  //   Which function
  //   ALU result
endmodule

module _11__CPU_D (
  output [7:0] Output
);

  wire button_1_out, button_2_out, decoder_1_out0, decoder_1_out1, decoder_1_out2, decoder_1_out3,
       decoder_1_out4, decoder_1_out5, decoder_1_out6, decoder_1_out7, not_1_out;
  wire [7:0] counter_1_q, multiplexer_1_out, multiplexer_2_out, multiplexer_3_out, register_1_q,
       register_2_q, register_3_q, register_4_q, register_5_q, register_6_q, register_7_q;
  wire [19:0] ram_1_data;

  Decoder #(.select(3), .enable("false")) decoder_1 (
    .out0(decoder_1_out0), .out1(decoder_1_out1), .out2(decoder_1_out2), .out3(decoder_1_out3),
    .out4(decoder_1_out4), .out5(decoder_1_out5), .out6(decoder_1_out6), .out7(decoder_1_out7),
    .sel(ram_1_data[3:1]));
  not not_1 (not_1_out, decoder_1_out7);
  Button button_1 (.out(button_1_out));
  Multiplexer #(.width(8), .enable("false")) multiplexer_1 (
    .in0(ram_1_data[11:4]), .in1(Output), .out(multiplexer_1_out), .sel(ram_1_data[0]));
  RAM #(.dataWidth(20)) ram_1 (.addr(counter_1_q), .data(ram_1_data));  // open: sel, clk, ld, clr
  Register register_1 (
    .D(multiplexer_1_out), .en(decoder_1_out0), .Q(register_1_q), .clk(button_1_out), .clr(button_2_out));
  Register register_2 (
    .D(multiplexer_1_out), .en(decoder_1_out1), .Q(register_2_q), .clk(button_1_out), .clr(button_2_out));
  Register register_3 (
    .D(multiplexer_1_out), .en(decoder_1_out2), .Q(register_3_q), .clk(button_1_out), .clr(button_2_out));
  Register register_4 (
    .D(multiplexer_1_out), .en(decoder_1_out3), .Q(register_4_q), .clk(button_1_out), .clr(button_2_out));
  Register register_5 (
    .D(multiplexer_1_out), .en(decoder_1_out4), .Q(register_5_q), .clk(button_1_out), .clr(button_2_out));
  Register register_6 (
    .D(multiplexer_1_out), .en(decoder_1_out5), .Q(register_6_q), .clk(button_1_out), .clr(button_2_out));
  Register register_7 (
    .D(multiplexer_1_out), .en(decoder_1_out6), .Q(register_7_q), .clk(button_1_out), .clr(button_2_out));
  Counter counter_1 (
    .load(decoder_1_out7), .D(multiplexer_1_out), .count(not_1_out), .Q(counter_1_q), .clk(button_1_out),
    .clr(button_2_out));  // open: carry
  Button button_2 (.out(button_2_out));
  Multiplexer #(.select(3), .width(8), .enable("false")) multiplexer_2 (
    .in0(register_1_q), .in1(register_2_q), .in2(register_3_q), .in3(register_4_q), .in4(register_5_q),
    .in5(register_6_q), .in6(register_7_q), .in7(counter_1_q), .out(multiplexer_2_out),
    .sel(ram_1_data[14:12]));
  Multiplexer #(.select(3), .width(8), .enable("false")) multiplexer_3 (
    .in0(register_1_q), .in1(register_2_q), .in2(register_3_q), .in3(register_4_q), .in4(register_5_q),
    .in5(register_6_q), .in6(register_7_q), .in7(counter_1_q), .out(multiplexer_3_out),
    .sel(ram_1_data[17:15]));
  _5__ALU u_5_alu_1 (.in_1(multiplexer_2_out), .in_2(ram_1_data[19:18]), .in_3(multiplexer_3_out), .out_4(Output));

  // Notes on the sheet:
  //   Clock signal
  //   Reset
  //   Jump statements
  //   It's register 7
  //   Let's treat the Program Counter as a normal register.
endmodule

module _12__ALU_2 (
  input  [7:0] in_1,
  input  [3:0] in_2,
  input  [7:0] _0__Plus,
  input  [7:0] in_4,
  input  [7:0] in_5,
  output [7:0] out_6
);

  wire comparator_1_eq, comparator_1_gt, comparator_1_lt, comparator_2_eq, comparator_2_gt, comparator_2_lt,
       not_1_out, or_2_out;
  wire [7:0] adder_1_out, adder_2_out, and_1_out, bit_extender_1_out, bit_extender_2_out, bit_extender_3_out,
       bit_extender_4_out, multiplexer_1_out, multiplexer_2_out, multiplexer_3_out, negator_1_out, or_1_out,
       subtractor_1_out;

  Adder adder_1 (.a(in_1), .b(_0__Plus), .out(adder_1_out));  // open: cin, cout
  Subtractor subtractor_1 (.a(in_1), .b(_0__Plus), .out(subtractor_1_out));  // open: bin, bout
  Negator negator_1 (.in(in_1), .out(negator_1_out));
  assign and_1_out = in_1 & _0__Plus;  // AND_Gate and_1, 8 bits wide
  assign or_1_out = in_1 | _0__Plus;  // OR_Gate or_1, 8 bits wide
  Comparator comparator_1 (.a(in_1), .b(_0__Plus), .gt(comparator_1_gt), .eq(comparator_1_eq), .lt(comparator_1_lt));
  Comparator comparator_2 (.a(in_1), .b(_0__Plus), .gt(comparator_2_gt), .eq(comparator_2_eq), .lt(comparator_2_lt));
  or or_2 (or_2_out, in_1[0], in_1[1], in_1[2], in_1[3], in_1[4], in_1[5], in_1[6], in_1[7]);
  not not_1 (not_1_out, or_2_out);
  Multiplexer #(.width(8)) multiplexer_1 (
    .in0(adder_2_out), .in1(in_4), .out(multiplexer_1_out), .sel(comparator_2_gt));  // open: en
  Multiplexer #(.width(8)) multiplexer_2 (
    .in0(adder_2_out), .in1(in_4), .out(multiplexer_2_out), .sel(comparator_2_eq));  // open: en
  Multiplexer #(.width(8)) multiplexer_3 (
    .in0(adder_2_out), .in1(in_4), .out(multiplexer_3_out), .sel(comparator_2_lt));  // open: en
  Adder adder_2 (.a(in_5), .b(8'h1), .out(adder_2_out));  // open: cin, cout
  assign bit_extender_1_out = {{7{1'b0}}, not_1_out};  // Bit_Extender bit_extender_1
  assign bit_extender_2_out = {{7{1'b0}}, comparator_1_gt};  // Bit_Extender bit_extender_2
  assign bit_extender_3_out = {{7{1'b0}}, comparator_1_eq};  // Bit_Extender bit_extender_3
  assign bit_extender_4_out = {{7{1'b0}}, comparator_1_lt};  // Bit_Extender bit_extender_4
  Multiplexer #(.select(4), .width(8), .enable("false")) multiplexer_4 (
    .in0(adder_1_out), .in1(subtractor_1_out), .in2(negator_1_out), .in3(in_1), .in4(and_1_out),
    .in5(or_1_out), .in6(bit_extender_1_out), .in7(bit_extender_2_out), .in8(bit_extender_3_out),
    .in9(bit_extender_4_out), .in10(multiplexer_1_out), .in11(multiplexer_2_out), .in12(multiplexer_3_out),
    .out(out_6), .sel(in_2));  // open: in13, in14, in15

  // Notes on the sheet:
  //   Reg A
  //   Reg B
  //   3: Pass through
  //   6: Boolean Inverter
  //   7: Greater than
  //   8: Equal
  //   9: Less than
  //   10: Jump if >
  //   11: Jump if =
  //   12: Jump if <
  //   1: Minus
  //   2: Negator
  //   4: And
  //   5: Or
  //   New PC value
  //   Old PC value
endmodule

module _13__CPU_E (
  output [7:0] Output
);

  wire button_1_out, button_2_out, decoder_1_out0, decoder_1_out1, decoder_1_out2, decoder_1_out3,
       decoder_1_out4, decoder_1_out5, decoder_1_out6, decoder_1_out7, not_1_out;
  wire [7:0] counter_1_q, multiplexer_1_out, multiplexer_2_out, multiplexer_3_out, multiplexer_4_out,
       register_1_q, register_2_q, register_3_q, register_4_q, register_5_q, register_6_q, register_7_q;
  wire [24:0] ram_1_data;

  Decoder #(.select(3), .enable("false")) decoder_1 (
    .out0(decoder_1_out0), .out1(decoder_1_out1), .out2(decoder_1_out2), .out3(decoder_1_out3),
    .out4(decoder_1_out4), .out5(decoder_1_out5), .out6(decoder_1_out6), .out7(decoder_1_out7),
    .sel(ram_1_data[3:1]));
  not not_1 (not_1_out, decoder_1_out7);
  Button button_1 (.out(button_1_out));
  Multiplexer #(.width(8), .enable("false")) multiplexer_1 (
    .in0(ram_1_data[11:4]), .in1(Output), .out(multiplexer_1_out), .sel(ram_1_data[0]));
  RAM #(.dataWidth(25)) ram_1 (.addr(counter_1_q), .data(ram_1_data));  // open: sel, clk, ld, clr
  Register register_1 (
    .D(multiplexer_1_out), .en(decoder_1_out0), .Q(register_1_q), .clk(button_1_out), .clr(button_2_out));
  Register register_2 (
    .D(multiplexer_1_out), .en(decoder_1_out1), .Q(register_2_q), .clk(button_1_out), .clr(button_2_out));
  Register register_3 (
    .D(multiplexer_1_out), .en(decoder_1_out2), .Q(register_3_q), .clk(button_1_out), .clr(button_2_out));
  Register register_4 (
    .D(multiplexer_1_out), .en(decoder_1_out3), .Q(register_4_q), .clk(button_1_out), .clr(button_2_out));
  Register register_5 (
    .D(multiplexer_1_out), .en(decoder_1_out4), .Q(register_5_q), .clk(button_1_out), .clr(button_2_out));
  Register register_6 (
    .D(multiplexer_1_out), .en(decoder_1_out5), .Q(register_6_q), .clk(button_1_out), .clr(button_2_out));
  Register register_7 (
    .D(multiplexer_1_out), .en(decoder_1_out6), .Q(register_7_q), .clk(button_1_out), .clr(button_2_out));
  Counter counter_1 (
    .load(decoder_1_out7), .D(multiplexer_1_out), .count(not_1_out), .Q(counter_1_q), .clk(button_1_out),
    .clr(button_2_out));  // open: carry
  Button button_2 (.out(button_2_out));
  Multiplexer #(.select(3), .width(8), .enable("false")) multiplexer_2 (
    .in0(register_1_q), .in1(register_2_q), .in2(register_3_q), .in3(register_4_q), .in4(register_5_q),
    .in5(register_6_q), .in6(register_7_q), .in7(counter_1_q), .out(multiplexer_2_out),
    .sel(ram_1_data[14:12]));
  Multiplexer #(.select(3), .width(8), .enable("false")) multiplexer_3 (
    .in0(register_1_q), .in1(register_2_q), .in2(register_3_q), .in3(register_4_q), .in4(register_5_q),
    .in5(register_6_q), .in6(register_7_q), .in7(counter_1_q), .out(multiplexer_3_out),
    .sel(ram_1_data[17:15]));
  Multiplexer #(.select(3), .width(8), .enable("false")) multiplexer_4 (
    .in0(register_1_q), .in1(register_2_q), .in2(register_3_q), .in3(register_4_q), .in4(register_5_q),
    .in5(register_6_q), .in6(register_7_q), .in7(counter_1_q), .out(multiplexer_4_out),
    .sel(ram_1_data[20:18]));
  _12__ALU_2 u_12_alu_2_1 (
    .in_1(multiplexer_2_out), .in_2(ram_1_data[24:21]), ._0__Plus(multiplexer_3_out),
    .in_4(multiplexer_4_out), .out_6(Output), .in_5(counter_1_q));

  // Notes on the sheet:
  //   Clock signal
  //   Reset
  //   Let's use our new ALU
  //   This lets us do conditional jumps
  //   and boolean evaluations
endmodule

module _14__CPU_F (
  output [7:0] Output
);

  wire and_1_out, button_1_out, button_2_out, button_3_out, decoder_1_out0, decoder_1_out1, decoder_1_out2,
       decoder_1_out3, decoder_1_out4, decoder_1_out5, decoder_1_out6, decoder_1_out7, not_1_out;
  wire [1:0] ram_1_data;
  wire [6:0] keyboard_1_data;
  wire [7:0] bit_extender_1_out, counter_1_q, multiplexer_1_out, multiplexer_2_out, multiplexer_3_out,
       multiplexer_4_out, register_1_q, register_2_q, register_3_q, register_4_q, register_5_q, register_6_q,
       register_7_q;
  wire [25:2] ram_1_data_2;

  Decoder #(.select(3), .enable("false")) decoder_1 (
    .out0(decoder_1_out0), .out1(decoder_1_out1), .out2(decoder_1_out2), .out3(decoder_1_out3),
    .out4(decoder_1_out4), .out5(decoder_1_out5), .out6(decoder_1_out6), .out7(decoder_1_out7),
    .sel(ram_1_data_2[4:2]));
  Keyboard keyboard_1 (.clk(button_2_out), .re(and_1_out), .clr(button_1_out), .data(keyboard_1_data));  // open: avail
  and and_1 (and_1_out, ram_1_data[0], ram_1_data[1]);
  Button button_1 (.out(button_1_out));
  not not_1 (not_1_out, decoder_1_out7);
  Button button_2 (.out(button_2_out));
  Multiplexer #(.select(2), .width(8), .enable("false")) multiplexer_1 (
    .in0(ram_1_data_2[12:5]), .in1(Output), .in3(bit_extender_1_out), .out(multiplexer_1_out),
    .sel(ram_1_data));  // open: in2
  RAM #(.dataWidth(26)) ram_1 (.addr(counter_1_q), .data({ram_1_data_2, ram_1_data}));  // open: sel, clk, ld, clr
  Register register_1 (
    .D(multiplexer_1_out), .en(decoder_1_out0), .Q(register_1_q), .clk(button_2_out), .clr(button_3_out));
  Register register_2 (
    .D(multiplexer_1_out), .en(decoder_1_out1), .Q(register_2_q), .clk(button_2_out), .clr(button_3_out));
  Register register_3 (
    .D(multiplexer_1_out), .en(decoder_1_out2), .Q(register_3_q), .clk(button_2_out), .clr(button_3_out));
  Register register_4 (
    .D(multiplexer_1_out), .en(decoder_1_out3), .Q(register_4_q), .clk(button_2_out), .clr(button_3_out));
  Register register_5 (
    .D(multiplexer_1_out), .en(decoder_1_out4), .Q(register_5_q), .clk(button_2_out), .clr(button_3_out));
  Register register_6 (
    .D(multiplexer_1_out), .en(decoder_1_out5), .Q(register_6_q), .clk(button_2_out), .clr(button_3_out));
  Register register_7 (
    .D(multiplexer_1_out), .en(decoder_1_out6), .Q(register_7_q), .clk(button_2_out), .clr(button_3_out));
  Counter counter_1 (
    .load(decoder_1_out7), .D(multiplexer_1_out), .count(not_1_out), .Q(counter_1_q), .clk(button_2_out),
    .clr(button_3_out));  // open: carry
  Button button_3 (.out(button_3_out));
  assign bit_extender_1_out = {{1{1'b0}}, keyboard_1_data};  // Bit_Extender bit_extender_1
  Multiplexer #(.select(3), .width(8), .enable("false")) multiplexer_2 (
    .in0(register_1_q), .in1(register_2_q), .in2(register_3_q), .in3(register_4_q), .in4(register_5_q),
    .in5(register_6_q), .in6(register_7_q), .in7(counter_1_q), .out(multiplexer_2_out),
    .sel(ram_1_data_2[15:13]));
  Multiplexer #(.select(3), .width(8), .enable("false")) multiplexer_3 (
    .in0(register_1_q), .in1(register_2_q), .in2(register_3_q), .in3(register_4_q), .in4(register_5_q),
    .in5(register_6_q), .in6(register_7_q), .in7(counter_1_q), .out(multiplexer_3_out),
    .sel(ram_1_data_2[18:16]));
  Multiplexer #(.select(3), .width(8), .enable("false")) multiplexer_4 (
    .in0(register_1_q), .in1(register_2_q), .in2(register_3_q), .in3(register_4_q), .in4(register_5_q),
    .in5(register_6_q), .in6(register_7_q), .in7(counter_1_q), .out(multiplexer_4_out),
    .sel(ram_1_data_2[21:19]));
  _12__ALU_2 u_12_alu_2_1 (
    .in_1(multiplexer_2_out), .in_2(ram_1_data_2[25:22]), ._0__Plus(multiplexer_3_out),
    .in_4(multiplexer_4_out), .out_6(Output), .in_5(counter_1_q));

  // Notes on the sheet:
  //   Let's add keyboard input
  //   Keyboard Buffer
  //   Clear buffer
  //   Clock signal
  //   Reset
endmodule

module _15__CPU_G (
  output [7:0] Output
);

  wire and_1_out, button_1_out, button_2_out, button_3_out, decoder_1_out0, decoder_1_out1, decoder_1_out2,
       decoder_1_out3, decoder_1_out4, decoder_1_out5, decoder_1_out6, decoder_1_out7, not_1_out;
  wire [1:0] ram_1_data;
  wire [6:0] keyboard_1_data;
  wire [7:0] bit_extender_1_out, counter_1_q, multiplexer_1_out, multiplexer_2_out, multiplexer_3_out,
       multiplexer_4_out, register_1_q, register_2_q, register_3_q, register_4_q, register_5_q, register_6_q;
  wire [25:2] ram_1_data_2;

  Decoder #(.select(3), .enable("false")) decoder_1 (
    .out0(decoder_1_out0), .out1(decoder_1_out1), .out2(decoder_1_out2), .out3(decoder_1_out3),
    .out4(decoder_1_out4), .out5(decoder_1_out5), .out6(decoder_1_out6), .out7(decoder_1_out7),
    .sel(ram_1_data_2[4:2]));
  Keyboard keyboard_1 (.clk(button_2_out), .re(and_1_out), .clr(button_1_out), .data(keyboard_1_data));  // open: avail
  and and_1 (and_1_out, ram_1_data[0], ram_1_data[1]);
  Button button_1 (.out(button_1_out));
  not not_1 (not_1_out, decoder_1_out7);
  Button button_2 (.out(button_2_out));
  Multiplexer #(.select(2), .width(8), .enable("false")) multiplexer_1 (
    .in1(Output), .in3(bit_extender_1_out), .out(multiplexer_1_out), .sel(ram_1_data));  // open: in0, in2
  RAM #(.dataWidth(26)) ram_1 (.addr(counter_1_q), .data({ram_1_data_2, ram_1_data}));  // open: sel, clk, ld, clr
  Register register_1 (
    .D(multiplexer_1_out), .en(decoder_1_out0), .Q(register_1_q), .clk(button_2_out), .clr(button_3_out));
  Register register_2 (
    .D(multiplexer_1_out), .en(decoder_1_out1), .Q(register_2_q), .clk(button_2_out), .clr(button_3_out));
  Register register_3 (
    .D(multiplexer_1_out), .en(decoder_1_out2), .Q(register_3_q), .clk(button_2_out), .clr(button_3_out));
  Register register_4 (
    .D(multiplexer_1_out), .en(decoder_1_out3), .Q(register_4_q), .clk(button_2_out), .clr(button_3_out));
  Register register_5 (
    .D(multiplexer_1_out), .en(decoder_1_out4), .Q(register_5_q), .clk(button_2_out), .clr(button_3_out));
  Register register_6 (
    .D(multiplexer_1_out), .en(decoder_1_out5), .Q(register_6_q), .clk(button_2_out), .clr(button_3_out));
  Counter counter_1 (
    .load(decoder_1_out7), .D(multiplexer_1_out), .count(not_1_out), .Q(counter_1_q), .clk(button_2_out),
    .clr(button_3_out));  // open: carry
  Button button_3 (.out(button_3_out));
  assign bit_extender_1_out = {{1{1'b0}}, keyboard_1_data};  // Bit_Extender bit_extender_1
  Multiplexer #(.select(3), .width(8), .enable("false")) multiplexer_2 (
    .in0(register_1_q), .in1(register_2_q), .in2(register_3_q), .in3(register_4_q), .in4(register_5_q),
    .in5(register_6_q), .in6(ram_1_data_2[12:5]), .in7(counter_1_q), .out(multiplexer_2_out),
    .sel(ram_1_data_2[15:13]));
  Multiplexer #(.select(3), .width(8), .enable("false")) multiplexer_3 (
    .in0(register_1_q), .in1(register_2_q), .in2(register_3_q), .in3(register_4_q), .in4(register_5_q),
    .in5(register_6_q), .in6(ram_1_data_2[12:5]), .in7(counter_1_q), .out(multiplexer_3_out),
    .sel(ram_1_data_2[18:16]));
  Multiplexer #(.select(3), .width(8), .enable("false")) multiplexer_4 (
    .in0(register_1_q), .in1(register_2_q), .in2(register_3_q), .in3(register_4_q), .in4(register_5_q),
    .in5(register_6_q), .in6(ram_1_data_2[12:5]), .in7(counter_1_q), .out(multiplexer_4_out),
    .sel(ram_1_data_2[21:19]));
  _12__ALU_2 u_12_alu_2_1 (
    .in_1(multiplexer_2_out), .in_2(ram_1_data_2[25:22]), ._0__Plus(multiplexer_3_out),
    .in_4(multiplexer_4_out), .out_6(Output), .in_5(counter_1_q));
  TTY tty_1 (.data(multiplexer_1_out[6:0]), .clk(button_2_out), .we(decoder_1_out6), .clr(button_3_out));

  // Notes on the sheet:
  //   Lets add screen output
  //   and treat the literal as a reg
  //   Keyboard Buffer
  //   Clear Buffer
  //   Clock signal
  //   Reset
endmodule

module _16__CPU_H (
);

  wire decoder_1_out0, decoder_1_out1, decoder_1_out2, decoder_1_out3, decoder_1_out4, decoder_1_out5,
       decoder_1_out6, decoder_1_out7, decoder_1_out8, decoder_1_out9, decoder_1_out10, decoder_1_out11,
       decoder_1_out12, decoder_1_out13, decoder_1_out14, decoder_1_out15, not_1_out, undriven_2, undriven_4,
       undriven_10;
  wire [3:0] undriven, undriven_5, undriven_6, undriven_7, undriven_8;
  wire [6:0] keyboard_1_data, multiplexer_4_out;
  wire [7:0] counter_1_q, multiplexer_1_out, multiplexer_2_out, multiplexer_3_out, n12_alu_2_1_out_6,
       ram_2_data, register_1_q, register_2_q, register_3_q, register_4_q, register_5_q, register_6_q,
       register_7_q, register_8_q, register_9_q, register_10_q, register_11_q, register_12_q, register_13_q,
       undriven_3;
  wire [7:7] multiplexer_4_out_2, undriven_9;
  wire [28:0] ram_1_data;

  Decoder #(.select(4), .enable("false")) decoder_1 (
    .out0(decoder_1_out0), .out1(decoder_1_out1), .out2(decoder_1_out2), .out3(decoder_1_out3),
    .out4(decoder_1_out4), .out5(decoder_1_out5), .out6(decoder_1_out6), .out7(decoder_1_out7),
    .out8(decoder_1_out8), .out9(decoder_1_out9), .out10(decoder_1_out10), .out11(decoder_1_out11),
    .out12(decoder_1_out12), .out13(decoder_1_out13), .out14(decoder_1_out14), .out15(decoder_1_out15),
    .sel(undriven));
  RAM #(.dataWidth(29)) ram_1 (.data(ram_1_data));  // open: addr, sel, clk, ld, clr
  Register register_1 (
    .D({multiplexer_4_out_2[7], multiplexer_4_out}), .en(decoder_1_out0), .Q(register_1_q), .clk(undriven_2),
    .clr(undriven_4));
  Register register_2 (
    .D({multiplexer_4_out_2[7], multiplexer_4_out}), .en(decoder_1_out2), .Q(register_2_q), .clk(undriven_2),
    .clr(undriven_4));
  Register register_3 (
    .D({multiplexer_4_out_2[7], multiplexer_4_out}), .en(decoder_1_out4), .Q(register_3_q), .clk(undriven_2),
    .clr(undriven_4));
  Register register_4 (.en(decoder_1_out6), .Q(register_4_q), .clk(undriven_2), .clr(undriven_4));  // open: D
  Register register_5 (
    .D({multiplexer_4_out_2[7], multiplexer_4_out}), .en(decoder_1_out8), .Q(register_5_q), .clk(undriven_2),
    .clr(undriven_4));
  Register register_6 (
    .D({multiplexer_4_out_2[7], multiplexer_4_out}), .en(decoder_1_out10), .Q(register_6_q),
    .clk(undriven_2), .clr(undriven_4));
  Register register_7 (
    .D({multiplexer_4_out_2[7], multiplexer_4_out}), .en(decoder_1_out12), .Q(register_7_q),
    .clk(undriven_2), .clr(undriven_4));
  not not_1 (not_1_out, decoder_1_out15);
  TTY tty_1 (.data(multiplexer_4_out), .clk(undriven_2), .we(decoder_1_out14), .clr(undriven_4));
  Register register_8 (
    .D({multiplexer_4_out_2[7], multiplexer_4_out}), .en(decoder_1_out1), .Q(register_8_q), .clk(undriven_2),
    .clr(undriven_4));
  Register register_9 (
    .D({multiplexer_4_out_2[7], multiplexer_4_out}), .en(decoder_1_out3), .Q(register_9_q), .clk(undriven_2),
    .clr(undriven_4));
  Register register_10 (
    .D({multiplexer_4_out_2[7], multiplexer_4_out}), .en(decoder_1_out5), .Q(register_10_q),
    .clk(undriven_2), .clr(undriven_4));
  Register register_11 (
    .D({multiplexer_4_out_2[7], multiplexer_4_out}), .en(decoder_1_out7), .Q(register_11_q),
    .clk(undriven_2), .clr(undriven_4));
  Register register_12 (
    .D({multiplexer_4_out_2[7], multiplexer_4_out}), .en(decoder_1_out9), .Q(register_12_q),
    .clk(undriven_2), .clr(undriven_4));
  Register register_13 (
    .D({multiplexer_4_out_2[7], multiplexer_4_out}), .en(decoder_1_out11), .Q(register_13_q),
    .clk(undriven_2), .clr(undriven_4));
  Counter counter_1 (
    .load(decoder_1_out15), .D({multiplexer_4_out_2[7], multiplexer_4_out}), .count(not_1_out),
    .Q(counter_1_q), .clk(undriven_2), .clr(undriven_4));  // open: carry
  Multiplexer #(.select(4), .width(8), .enable("false")) multiplexer_1 (
    .in0(register_1_q), .in1(register_8_q), .in2(register_2_q), .in3(register_9_q), .in4(register_3_q),
    .in5(register_10_q), .in6(register_4_q), .in7(register_11_q), .in8(register_5_q), .in9(register_12_q),
    .in10(register_6_q), .in11(register_13_q), .in12(register_7_q), .in13(ram_2_data), .in14(undriven_3),
    .in15(counter_1_q), .out(multiplexer_1_out), .sel(undriven_5));
  Multiplexer #(.select(4), .width(8), .enable("false")) multiplexer_2 (
    .in0(register_1_q), .in1(register_8_q), .in2(register_2_q), .in3(register_9_q), .in4(register_3_q),
    .in5(register_10_q), .in6(register_4_q), .in7(register_11_q), .in8(register_5_q), .in9(register_12_q),
    .in10(register_6_q), .in11(register_13_q), .in12(register_7_q), .in13(ram_2_data), .in14(undriven_3),
    .in15(counter_1_q), .out(multiplexer_2_out), .sel(undriven_6));
  Multiplexer #(.select(4), .width(8), .enable("false")) multiplexer_3 (
    .in0(register_1_q), .in1(register_8_q), .in2(register_2_q), .in3(register_9_q), .in4(register_3_q),
    .in5(register_10_q), .in6(register_4_q), .in7(register_11_q), .in8(register_5_q), .in9(register_12_q),
    .in10(register_6_q), .in11(register_13_q), .in12(register_7_q), .in13(ram_2_data), .in14(undriven_3),
    .in15(counter_1_q), .out(multiplexer_3_out), .sel(undriven_7));
  RAM #(.bus("separate")) ram_2 (
    .addr({multiplexer_4_out_2[7], multiplexer_4_out}), .din(register_7_q), .data(ram_2_data),
    .str(decoder_1_out13), .clk(undriven_2), .clr(undriven_4));  // open: sel, ld
  Keyboard keyboard_1 (.clk(undriven_2), .re(undriven_10), .clr(undriven_4), .data(keyboard_1_data));  // open: avail
  _12__ALU_2 u_12_alu_2_1 (
    .in_1(multiplexer_1_out), .in_2(undriven_8), ._0__Plus(multiplexer_2_out), .in_4(multiplexer_3_out),
    .out_6(n12_alu_2_1_out_6), .in_5(counter_1_q));
  Multiplexer #(.width(8), .enable("false")) multiplexer_4 (
    .in0(n12_alu_2_1_out_6), .in1({undriven_9[7], keyboard_1_data}),
    .out({multiplexer_4_out_2[7], multiplexer_4_out}), .sel(undriven_10));

  // Notes on the sheet:
  //   reg to load
  //   0
  //   2
  //   4
  //   6
  //   8
  //   10
  //   12
  //   1
  //   3
  //   5
  //   7
  //   9
  //   11
  //   15
  //   14
  //   Keyboard Buffer
  //   14(op code literal)
  //   Func
  //   Args 1,2,3
  //   PC
  //   ALU or keyboard
  //   13
  //   RAM
endmodule
