// Logisim project pres2.circ as structural Verilog: 2 circuits, main circuit 12. ALU 2
module _12__ALU_2 (
  input  [7:0] in_1,
  input  [3:0] in_2,
  input  [7:0] _0__Plus,
  input  [7:0] in_4,
  input  [7:0] in_5,
  output [7:0] out_6
);

  wire comparator_1_eq, comparator_1_gt, comparator_1_lt, comparator_2_eq, comparator_2_gt, comparator_2_lt,
       not_1_out, or_2_out;
  wire [7:0] adder_1_out, adder_2_out, and_1_out, bit_extender_1_out, bit_extender_2_out, bit_extender_3_out,
       bit_extender_4_out, multiplexer_1_out, multiplexer_2_out, multiplexer_3_out, negator_1_out, or_1_out,
       subtractor_1_out;

  Adder adder_1 (.a(in_1), .b(_0__Plus), .out(adder_1_out));  // open: cin, cout
  Subtractor subtractor_1 (.a(in_1), .b(_0__Plus), .out(subtractor_1_out));  // open: bin, bout
  Negator negator_1 (.in(in_1), .out(negator_1_out));
  assign and_1_out = in_1 & _0__Plus;  // AND_Gate and_1, 8 bits wide
  assign or_1_out = in_1 | _0__Plus;  // OR_Gate or_1, 8 bits wide
  Comparator comparator_1 (.a(in_1), .b(_0__Plus), .gt(comparator_1_gt), .eq(comparator_1_eq), .lt(comparator_1_lt));
  Comparator comparator_2 (.a(in_1), .b(_0__Plus), .gt(comparator_2_gt), .eq(comparator_2_eq), .lt(comparator_2_lt));
  or or_2 (or_2_out, in_1[0], in_1[1], in_1[2], in_1[3], in_1[4], in_1[5], in_1[6], in_1[7]);
  not not_1 (not_1_out, or_2_out);
  Multiplexer #(.width(8)) multiplexer_1 (
    .in0(adder_2_out), .in1(in_4), .out(multiplexer_1_out), .sel(comparator_2_gt));  // open: en
  Multiplexer #(.width(8)) multiplexer_2 (
    .in0(adder_2_out), .in1(in_4), .out(multiplexer_2_out), .sel(comparator_2_eq));  // open: en
  Multiplexer #(.width(8)) multiplexer_3 (
    .in0(adder_2_out), .in1(in_4), .out(multiplexer_3_out), .sel(comparator_2_lt));  // open: en
  Adder adder_2 (.a(in_5), .b(8'h1), .out(adder_2_out));  // open: cin, cout
  assign bit_extender_1_out = {{7{1'b0}}, not_1_out};  // Bit_Extender bit_extender_1
  assign bit_extender_2_out = {{7{1'b0}}, comparator_1_gt};  // Bit_Extender bit_extender_2
  assign bit_extender_3_out = {{7{1'b0}}, comparator_1_eq};  // Bit_Extender bit_extender_3
  assign bit_extender_4_out = {{7{1'b0}}, comparator_1_lt};  // Bit_Extender bit_extender_4
  Multiplexer #(.select(4), .width(8), .enable("false")) multiplexer_4 (
    .in0(adder_1_out), .in1(subtractor_1_out), .in2(negator_1_out), .in3(in_1), .in4(and_1_out),
    .in5(or_1_out), .in6(bit_extender_1_out), .in7(bit_extender_2_out), .in8(bit_extender_3_out),
    .in9(bit_extender_4_out), .in10(multiplexer_1_out), .in11(multiplexer_2_out), .in12(multiplexer_3_out),
    .out(out_6), .sel(in_2));  // open: in13, in14, in15

  // Notes on the sheet:
  //   Reg A
  //   Reg B
  //   3: Pass through
  //   6: Boolean Inverter
  //   7: Greater than
  //   8: Equal
  //   9: Less than
  //   10: Jump if >
  //   11: Jump if =
  //   12: Jump if <
  //   1: Minus
  //   2: Negator
  //   4: And
  //   5: Or
  //   New PC value
  //   Old PC value
endmodule

module _16__CPU_H (
);

  wire button_1_out, button_2_out, decoder_1_out0, decoder_1_out1, decoder_1_out2, decoder_1_out3,
       decoder_1_out4, decoder_1_out5, decoder_1_out6, decoder_1_out7, decoder_1_out8, decoder_1_out9,
       decoder_1_out10, decoder_1_out11, decoder_1_out12, decoder_1_out13, decoder_1_out14, decoder_1_out15,
       not_1_out;
  wire [3:0] ram_1_data_2, ram_1_data_3, ram_1_data_4;
  wire [6:0] keyboard_1_data, multiplexer_4_out;
  wire [7:0] counter_1_q, multiplexer_1_out, multiplexer_2_out, multiplexer_3_out, n12_alu_2_1_out_6,
       ram_2_data, register_1_q, register_2_q, register_3_q, register_4_q, register_5_q, register_6_q,
       register_7_q, register_8_q, register_9_q, register_10_q, register_11_q, register_12_q, register_13_q;
  wire [7:7] multiplexer_4_out_2;
  wire [28:0] ram_1_data;

  Decoder #(.select(4), .enable("false")) decoder_1 (
    .out0(decoder_1_out0), .out1(decoder_1_out1), .out2(decoder_1_out2), .out3(decoder_1_out3),
    .out4(decoder_1_out4), .out5(decoder_1_out5), .out6(decoder_1_out6), .out7(decoder_1_out7),
    .out8(decoder_1_out8), .out9(decoder_1_out9), .out10(decoder_1_out10), .out11(decoder_1_out11),
    .out12(decoder_1_out12), .out13(decoder_1_out13), .out14(decoder_1_out14), .out15(decoder_1_out15),
    .sel(ram_1_data_2));
  RAM #(.dataWidth(29)) ram_1 (
    .addr(counter_1_q),
    .data({ram_1_data[28:24], ram_1_data_4, ram_1_data_3, ram_1_data[15:12], ram_1_data_2, ram_1_data[7:0]}));  // open: sel, clk, ld, clr
  Button button_1 (.out(button_1_out));
  Register register_1 (
    .D({multiplexer_4_out_2[7], multiplexer_4_out}), .en(decoder_1_out0), .Q(register_1_q),
    .clk(button_1_out), .clr(button_2_out));
  Register register_2 (
    .D({multiplexer_4_out_2[7], multiplexer_4_out}), .en(decoder_1_out2), .Q(register_2_q),
    .clk(button_1_out), .clr(button_2_out));
  Register register_3 (
    .D({multiplexer_4_out_2[7], multiplexer_4_out}), .en(decoder_1_out4), .Q(register_3_q),
    .clk(button_1_out), .clr(button_2_out));
  Register register_4 (.en(decoder_1_out6), .Q(register_4_q), .clk(button_1_out), .clr(button_2_out));  // open: D
  Register register_5 (
    .D({multiplexer_4_out_2[7], multiplexer_4_out}), .en(decoder_1_out8), .Q(register_5_q),
    .clk(button_1_out), .clr(button_2_out));
  Register register_6 (
    .D({multiplexer_4_out_2[7], multiplexer_4_out}), .en(decoder_1_out10), .Q(register_6_q),
    .clk(button_1_out), .clr(button_2_out));
  Register register_7 (
    .D({multiplexer_4_out_2[7], multiplexer_4_out}), .en(decoder_1_out12), .Q(register_7_q),
    .clk(button_1_out), .clr(button_2_out));
  not not_1 (not_1_out, decoder_1_out15);
  TTY tty_1 (.data(multiplexer_4_out), .clk(button_1_out), .we(decoder_1_out14), .clr(button_2_out));
  Register register_8 (
    .D({multiplexer_4_out_2[7], multiplexer_4_out}), .en(decoder_1_out1), .Q(register_8_q),
    .clk(button_1_out), .clr(button_2_out));
  Register register_9 (
    .D({multiplexer_4_out_2[7], multiplexer_4_out}), .en(decoder_1_out3), .Q(register_9_q),
    .clk(button_1_out), .clr(button_2_out));
  Register register_10 (
    .D({multiplexer_4_out_2[7], multiplexer_4_out}), .en(decoder_1_out5), .Q(register_10_q),
    .clk(button_1_out), .clr(button_2_out));
  Register register_11 (
    .D({multiplexer_4_out_2[7], multiplexer_4_out}), .en(decoder_1_out7), .Q(register_11_q),
    .clk(button_1_out), .clr(button_2_out));
  Register register_12 (
    .D({multiplexer_4_out_2[7], multiplexer_4_out}), .en(decoder_1_out9), .Q(register_12_q),
    .clk(button_1_out), .clr(button_2_out));
  Register register_13 (
    .D({multiplexer_4_out_2[7], multiplexer_4_out}), .en(decoder_1_out11), .Q(register_13_q),
    .clk(button_1_out), .clr(button_2_out));
  Counter counter_1 (
    .load(decoder_1_out15), .D({multiplexer_4_out_2[7], multiplexer_4_out}), .count(not_1_out),
    .Q(counter_1_q), .clk(button_1_out), .clr(button_2_out));  // open: carry
  Multiplexer #(.select(4), .width(8), .enable("false")) multiplexer_1 (
    .in0(register_1_q), .in1(register_8_q), .in2(register_2_q), .in3(register_9_q), .in4(register_3_q),
    .in5(register_10_q), .in6(register_4_q), .in7(register_11_q), .in8(register_5_q), .in9(register_12_q),
    .in10(register_6_q), .in11(register_13_q), .in12(register_7_q), .in13(ram_2_data),
    .in14(ram_1_data[7:0]), .in15(counter_1_q), .out(multiplexer_1_out), .sel(ram_1_data_4));
  Multiplexer #(.select(4), .width(8), .enable("false")) multiplexer_2 (
    .in0(register_1_q), .in1(register_8_q), .in2(register_2_q), .in3(register_9_q), .in4(register_3_q),
    .in5(register_10_q), .in6(register_4_q), .in7(register_11_q), .in8(register_5_q), .in9(register_12_q),
    .in10(register_6_q), .in11(register_13_q), .in12(register_7_q), .in13(ram_2_data),
    .in14(ram_1_data[7:0]), .in15(counter_1_q), .out(multiplexer_2_out), .sel(ram_1_data_3));
  Multiplexer #(.select(4), .width(8), .enable("false")) multiplexer_3 (
    .in0(register_1_q), .in1(register_8_q), .in2(register_2_q), .in3(register_9_q), .in4(register_3_q),
    .in5(register_10_q), .in6(register_4_q), .in7(register_11_q), .in8(register_5_q), .in9(register_12_q),
    .in10(register_6_q), .in11(register_13_q), .in12(register_7_q), .in13(ram_2_data),
    .in14(ram_1_data[7:0]), .in15(counter_1_q), .out(multiplexer_3_out), .sel(ram_1_data[15:12]));
  RAM #(.bus("separate")) ram_2 (
    .addr(register_7_q), .din({multiplexer_4_out_2[7], multiplexer_4_out}), .data(ram_2_data),
    .str(decoder_1_out13), .clk(button_1_out), .clr(button_2_out));  // open: sel, ld
  Keyboard keyboard_1 (.clk(button_1_out), .clr(button_2_out), .data(keyboard_1_data));  // open: re, avail
  Button button_2 (.out(button_2_out));
  _12__ALU_2 u_12_alu_2_1 (
    .in_1(multiplexer_1_out), .in_2(ram_1_data[27:24]), ._0__Plus(multiplexer_2_out),
    .in_4(multiplexer_3_out), .out_6(n12_alu_2_1_out_6), .in_5(counter_1_q));
  Multiplexer #(.width(8), .enable("false")) multiplexer_4 (
    .in0(n12_alu_2_1_out_6), .in1({1'b0, keyboard_1_data}),
    .out({multiplexer_4_out_2[7], multiplexer_4_out}), .sel(ram_1_data[28]));

  // Notes on the sheet:
  //   Program Memory
  //   Clock
  //   0
  //   2
  //   4
  //   6
  //   8
  //   10
  //   12
  //   14
  //   1
  //   3
  //   5
  //   7
  //   9
  //   11
  //   15
  //   13
  //   RAM
  //   Clear
endmodule
