// Logisim project Lesson1.circ as structural Verilog: 4 circuits, main circuit aLogicGates
module aLogicGates (
  input  in_1,
  input  in_2,
  input  in_3,
  input  NOT_Gate,
  input  OR_Gate,
  input  in_6,
  input  in_7,
  input  in_8,
  input  [2:0] in_9,
  input  [3:0] in_10,
  input  [3:0] in_11,
  input  [3:0] in_12,
  output out_13,
  output out_14,
  output out_15,
  output out_16,
  output out_17,
  output [2:0] out_18,
  output [1:0] out_19,
  output [1:0] out_20,
  output [3:0] out_21,
  output out_22
);

  assign out_21 = in_11 & in_12;  // AND_Gate and_1, 4 bits wide
  Button button_1 (.out(out_22));
  and and_2 (out_14, in_2, in_3);
  not not_1 (out_15, NOT_Gate);
  or or_1 (out_16, OR_Gate, in_6);
  nand nand_1 (out_17, in_7, in_8);

  assign out_13 = in_1;
  assign out_18 = in_9;
  assign out_19 = in_10[1:0];
  assign out_20 = in_10[3:2];

  // Notes on the sheet:
  //   Input pint (square)
  //   AND Gate
  //   NAND Gate
  //   Bundled Pins/Wires
  //   Splitter
  //   Gates can take in wire bundles
  //   Button
  //   Output pin (round)
  //   Correspond to pins on microchips
  //   Google DIP chips
  //   Groups together or splits apart wire bundles
  //   Input and output bundles bust have same number of wires
endmodule

module bFlipFlop (
  input  Data,
  input  GateKeeper,
  input  Data_2,
  input  GateKeeper_2,
  input  Data_3,
  input  Gatekeeper_Clock,
  output out_7,
  output out_8,
  output out_9
);

  wire nand_1_out, nand_2_out, nand_3_out, nand_4_out, nand_7_out, nand_9_out, nand_11_out, nand_13_out,
       nand_14_out, nand_17_out, not_1_out, not_2_out, not_3_out;

  not not_1 (not_1_out, GateKeeper);
  not not_2 (not_2_out, GateKeeper_2);
  D_Flip_Flop d_ff_1 (.D(Data_3), .clk(Gatekeeper_Clock), .Q(out_9));  // open: Qn, preset, reset
  nand nand_1 (nand_1_out, Data, not_1_out);
  nand nand_2 (nand_2_out, nand_1_out, not_1_out);
  nand nand_3 (nand_3_out, Data_2, not_2_out);
  nand nand_4 (nand_4_out, nand_3_out, not_2_out);
  nand nand_5 (out_7, nand_1_out, nand_7_out);
  nand nand_6 (out_7, nand_1_out, nand_7_out);
  nand nand_7 (nand_7_out, out_7, nand_2_out);
  nand nand_8 (nand_7_out, out_7, nand_2_out);
  nand nand_9 (nand_9_out, nand_3_out, nand_11_out);
  nand nand_10 (nand_9_out, nand_3_out, nand_11_out);
  nand nand_11 (nand_11_out, nand_9_out, nand_4_out);
  nand nand_12 (nand_11_out, nand_9_out, nand_4_out);
  not not_3 (not_3_out, not_2_out);
  nand nand_13 (nand_13_out, nand_9_out, not_3_out);
  nand nand_14 (nand_14_out, nand_13_out, not_3_out);
  nand nand_15 (out_8, nand_13_out, nand_17_out);
  nand nand_16 (out_8, nand_13_out, nand_17_out);
  nand nand_17 (nand_17_out, out_8, nand_14_out);
  nand nand_18 (nand_17_out, out_8, nand_14_out);

  // Notes on the sheet:
  //   1:pass through
  //   0:remember value
  //   (Little Triangle)
  //   Remembers on rising edge (what's that?)
  //   Lets put it in a box!!
  //   We can arrange NAND gates in a way that has memory
  //   Remembered Value
endmodule

module cRegister (
  input  [3:0] Input,
  input  [3:0] in_2,
  output [3:0] Output,
  output [3:0] out_4
);

  wire button_1_out, button_2_out;

  Register #(.width(4)) register_1 (.D(in_2), .clk(button_1_out), .Q(out_4));  // open: en, clr
  Button button_1 (.out(button_1_out));
  Button button_2 (.out(button_2_out));
  D_Flip_Flop d_ff_1 (.D(Input[0]), .clk(button_2_out), .Q(Output[0]));  // open: Qn, preset, reset
  D_Flip_Flop d_ff_2 (.D(Input[1]), .clk(button_2_out), .Q(Output[1]));  // open: Qn, preset, reset
  D_Flip_Flop d_ff_3 (.D(Input[2]), .clk(button_2_out), .Q(Output[2]));  // open: Qn, preset, reset
  D_Flip_Flop d_ff_4 (.D(Input[3]), .clk(button_2_out), .Q(Output[3]));  // open: Qn, preset, reset

  // Notes on the sheet:
  //   Multiple flip flops can form a Register
  //   Lets put it in a box!!!
  //   Clock
endmodule

module dMultiplexer (
  input  _0,
  input  _1,
  input  in_3,
  input  in_4,
  input  in_5,
  input  in_6,
  input  in_7,
  input  in_8,
  input  in_9,
  input  [3:0] in_10,
  input  [3:0] in_11,
  input  in_12,
  output Output,
  output out_14,
  output out_15,
  output [3:0] out_16
);

  wire and_1_out, and_2_out, multiplexer_1_out, multiplexer_2_out, not_1_out;

  Multiplexer #(.enable("false")) multiplexer_1 (.in0(in_6), .in1(in_7), .out(multiplexer_1_out), .sel(in_4));
  Multiplexer #(.enable("false")) multiplexer_2 (.in0(in_8), .in1(in_9), .out(multiplexer_2_out), .sel(in_4));
  not not_1 (not_1_out, in_3);
  Multiplexer #(.enable("false")) multiplexer_3 (.in0(_0), .in1(_1), .out(out_14), .sel(in_3));
  Multiplexer #(.width(4), .enable("false")) multiplexer_4 (.in0(in_10), .in1(in_11), .out(out_16), .sel(in_12));
  and and_1 (and_1_out, _0, not_1_out);
  and and_2 (and_2_out, _1, in_3);
  Multiplexer #(.enable("false")) multiplexer_5 (
    .in0(multiplexer_1_out), .in1(multiplexer_2_out), .out(out_15), .sel(in_5));
  or or_1 (Output, and_1_out, and_2_out);

  // Notes on the sheet:
  //   Data Inputs
  //   Questions:
  //   Muxs can have wire bundles as inputs
  //   Multiplexers let you choose which of several inputs to output
  //   Let's put it in a box!!!
  //   4-input mux made out of 2-input muxs
  //   If we made an 8 input mux out of 2 input muxs, how many would we need?
  //   If we want to choose between 8 data inputs, how many select bits do we need?
endmodule
