// Logisim project Lesson2.circ as structural Verilog: 5 circuits, main circuit aALU
module aALU (
  input  [7:0] Arguments,
  input  [1:0] in_2,
  input  [7:0] in_3,
  output [7:0] Output
);

  wire [7:0] adder_1_out, negator_1_out, subtractor_1_out;

  Adder adder_1 (.a(Arguments), .b(in_3), .out(adder_1_out));  // open: cin, cout
  Subtractor subtractor_1 (.a(Arguments), .b(in_3), .out(subtractor_1_out));  // open: bin, bout
  Negator negator_1 (.in(Arguments), .out(negator_1_out));
  Multiplexer #(.select(2), .width(8), .enable("false")) multiplexer_1 (
    .in0(adder_1_out), .in1(subtractor_1_out), .in2(negator_1_out), .in3(Arguments), .out(Output), .sel(in_2));

  // Notes on the sheet:
  //   Arithmetic Logic Unit
  //   0: Addition
  //   1: Subtraction
  //   2: Negation
  //   3: Pass through
  //   What if the inputs to a mux were mathimatical functions?
  //   It's not that hard though. We can talk about it latter at another time
  //   Function selector
  //   The methods to design the additon/subtraction/ect blocks are beyond the scope of this presentation
endmodule

module bMathMachine (
  input  [7:0] in_1,
  input  [7:0] in_2,
  input  [1:0] in_3,
  input  [1:0] in_4,
  input  [1:0] in_5,
  input  [7:0] in_6,
  input  [7:0] in_7,
  output [7:0] out_8
);

  wire button_1_out, button_2_out, button_3_out, button_4_out;
  wire [7:0] multiplexer_1_out, multiplexer_2_out, register_1_q, register_2_q, register_3_q, register_4_q;

  Register register_1 (.D(in_1), .clk(button_1_out), .Q(register_1_q));  // open: en, clr
  Button button_1 (.out(button_1_out));
  Register register_2 (.D(in_2), .clk(button_2_out), .Q(register_2_q));  // open: en, clr
  Button button_2 (.out(button_2_out));
  Register register_3 (.D(in_6), .clk(button_3_out), .Q(register_3_q));  // open: en, clr
  Button button_3 (.out(button_3_out));
  Register register_4 (.D(in_7), .clk(button_4_out), .Q(register_4_q));  // open: en, clr
  Button button_4 (.out(button_4_out));
  Multiplexer #(.select(2), .width(8), .enable("false")) multiplexer_1 (
    .in0(register_1_q), .in1(register_2_q), .in2(register_3_q), .in3(register_4_q), .out(multiplexer_1_out),
    .sel(in_3));
  Multiplexer #(.select(2), .width(8), .enable("false")) multiplexer_2 (
    .in0(register_1_q), .in1(register_2_q), .in2(register_3_q), .in3(register_4_q), .out(multiplexer_2_out),
    .sel(in_4));
  aALU aalu_1 (.Output(out_8), .in_3(multiplexer_2_out), .in_2(in_5), .Arguments(multiplexer_1_out));

  // Notes on the sheet:
  //   Load
  //   Load
  //   Load
  //   Load
  //   We can use muxs to choose which arguments are sent into the ALU
  //   Argument Selection
  //   Note: This ^ is a common "Bus" wiring layout
  //   2: Negate A
  //   Function Selection
  //   0: Addition A+B
  //   1: Subtraction A-B
  //   3: Pass Through A
  //   Question: Compute 3+5-4
endmodule

module cDecoder (
  input  in_1,
  input  in_2,
  output out_3,
  output out_4,
  output out_5,
  output out_6,
  output out_7,
  output out_8,
  output out_9,
  output out_10
);

  wire not_1_out, not_2_out, not_3_out, not_4_out;

  not not_1 (not_1_out, in_1);
  not not_2 (not_2_out, in_2);
  not not_3 (not_3_out, in_1);
  not not_4 (not_4_out, in_2);
  Decoder #(.select(2)) decoder_1 (
    .out0(out_7), .out1(out_8), .out2(out_9), .out3(out_10), .sel({in_1, in_2}));  // open: en
  and and_1 (out_3, not_1_out, not_2_out);
  and and_2 (out_4, not_3_out, in_2);
  and and_3 (out_5, in_1, not_4_out);
  and and_4 (out_6, in_1, in_2);

  // Notes on the sheet:
  //   Lets put it in a box!!!
  //   Decoder: Turn on the wire corresponding to the input number
endmodule

module dLoadMultipleRegisters (
  input  [1:0] Which_register,
  input  [7:0] Data_to_store
);

  wire button_1_out, button_2_out, decoder_1_out0, decoder_1_out1, decoder_1_out2, decoder_1_out3;

  Decoder #(.select(2), .enable("false")) decoder_1 (
    .out0(decoder_1_out0), .out1(decoder_1_out1), .out2(decoder_1_out2), .out3(decoder_1_out3),
    .sel(Which_register));
  Register register_1 (.D(Data_to_store), .en(decoder_1_out0), .clk(button_1_out), .clr(button_2_out));  // open: Q
  Register register_2 (.D(Data_to_store), .en(decoder_1_out1), .clk(button_1_out), .clr(button_2_out));  // open: Q
  Register register_3 (.D(Data_to_store), .en(decoder_1_out2), .clk(button_1_out), .clr(button_2_out));  // open: Q
  Register register_4 (.D(Data_to_store), .en(decoder_1_out3), .clk(button_1_out), .clr(button_2_out));  // open: Q
  Button button_1 (.out(button_1_out));
  Button button_2 (.out(button_2_out));

  // Notes on the sheet:
  //   gets loaded?
  //   We can use a Decoder to choose which register gets loaded
  //   Clock/Load
  //   Reset
endmodule

module eMultiLoadAndSelect (
  input  [1:0] Which_register,
  input  [7:0] Data_to_store,
  input  [1:0] in_3,
  input  [1:0] in_4,
  input  [1:0] in_5,
  output [7:0] out_6
);

  wire button_1_out, decoder_1_out0, decoder_1_out1, decoder_1_out2, decoder_1_out3;
  wire [7:0] multiplexer_1_out, multiplexer_2_out, register_1_q, register_2_q, register_3_q, register_4_q;

  Decoder #(.select(2), .enable("false")) decoder_1 (
    .out0(decoder_1_out0), .out1(decoder_1_out1), .out2(decoder_1_out2), .out3(decoder_1_out3),
    .sel(Which_register));
  Button button_1 (.out(button_1_out));
  Register register_1 (.D(Data_to_store), .en(decoder_1_out0), .clk(button_1_out), .Q(register_1_q));  // open: clr
  Register register_2 (.D(Data_to_store), .en(decoder_1_out1), .clk(button_1_out), .Q(register_2_q));  // open: clr
  Register register_3 (.D(Data_to_store), .en(decoder_1_out2), .clk(button_1_out), .Q(register_3_q));  // open: clr
  Register register_4 (.D(Data_to_store), .en(decoder_1_out3), .clk(button_1_out), .Q(register_4_q));  // open: clr
  Multiplexer #(.select(2), .width(8), .enable("false")) multiplexer_1 (
    .in0(register_1_q), .in1(register_2_q), .in2(register_3_q), .in3(register_4_q), .out(multiplexer_1_out),
    .sel(in_3));
  Multiplexer #(.select(2), .width(8), .enable("false")) multiplexer_2 (
    .in0(register_1_q), .in1(register_2_q), .in2(register_3_q), .in3(register_4_q), .out(multiplexer_2_out),
    .sel(in_4));
  aALU aalu_1 (.Output(out_6), .in_3(multiplexer_2_out), .in_2(in_5), .Arguments(multiplexer_1_out));

  // Notes on the sheet:
  //   gets loaded?
  //   Lets put the multi loading and selection parts together
  //   Clock/Load
  //   Argument Selection
  //   Function Selection
endmodule
