// Logisim project Lesson3.circ as structural Verilog: 1 circuit, main circuit alu
module alu (
  input  [7:0] Reg_A,
  input  [3:0] in_2,
  input  [3:0] in_3,
  input  [7:0] in_4,
  input  [7:0] in_5,
  input  [7:0] New_PC_value,
  input  [7:0] New_PC_value_2,
  input  [7:0] in_8,
  input  [7:0] in_9,
  output [7:0] ALU_output,
  output [7:0] ALU_output_2
);

  wire adder_1_cout, adder_3_cout, comparator_1_eq, comparator_1_gt, comparator_1_lt, comparator_3_eq,
       comparator_3_gt, comparator_3_lt, or_3_out, subtractor_1_bout, undriven, undriven_2, undriven_3;
  wire [7:0] adder_1_out, adder_3_out, and_1_out, bit_extender_1_out, bit_extender_3_out, bit_extender_5_out,
       bit_extender_7_out, multiplexer_1_out, multiplexer_3_out, multiplexer_5_out, negator_1_out, or_1_out,
       subtractor_1_out, undriven_4, undriven_5, undriven_6;

  Adder adder_1 (.a(Reg_A), .b(in_4), .out(adder_1_out), .cin(undriven), .cout(adder_1_cout));
  Adder adder_2 (.a(Reg_A), .b(in_4), .out(adder_1_out), .cin(undriven), .cout(adder_1_cout));
  Subtractor subtractor_1 (.a(Reg_A), .b(in_4), .out(subtractor_1_out), .bin(undriven_2), .bout(subtractor_1_bout));
  Subtractor subtractor_2 (.a(Reg_A), .b(in_4), .out(subtractor_1_out), .bin(undriven_2), .bout(subtractor_1_bout));
  Negator negator_1 (.in(Reg_A), .out(negator_1_out));
  Negator negator_2 (.in(Reg_A), .out(negator_1_out));
  assign and_1_out = Reg_A & in_4;  // AND_Gate and_1, 8 bits wide
  assign and_1_out = Reg_A & in_4;  // AND_Gate and_2, 8 bits wide
  assign or_1_out = Reg_A | in_4;  // OR_Gate or_1, 8 bits wide
  assign or_1_out = Reg_A | in_4;  // OR_Gate or_2, 8 bits wide
  Comparator comparator_1 (.a(Reg_A), .b(in_4), .gt(comparator_1_gt), .eq(comparator_1_eq), .lt(comparator_1_lt));
  Comparator comparator_2 (.a(Reg_A), .b(in_4), .gt(comparator_1_gt), .eq(comparator_1_eq), .lt(comparator_1_lt));
  or or_3 (or_3_out, Reg_A[0], Reg_A[1], Reg_A[2], Reg_A[3], Reg_A[4], Reg_A[5], Reg_A[6], Reg_A[7]);
  or or_4 (or_3_out, Reg_A[0], Reg_A[1], Reg_A[2], Reg_A[3], Reg_A[4], Reg_A[5], Reg_A[6], Reg_A[7]);
  Comparator comparator_3 (.a(Reg_A), .b(in_4), .gt(comparator_3_gt), .eq(comparator_3_eq), .lt(comparator_3_lt));
  Comparator comparator_4 (.a(Reg_A), .b(in_4), .gt(comparator_3_gt), .eq(comparator_3_eq), .lt(comparator_3_lt));
  Adder adder_3 (.a(in_8), .b(8'h1), .out(adder_3_out), .cin(undriven_3), .cout(adder_3_cout));
  Adder adder_4 (.a(in_8), .b(8'h1), .out(adder_3_out), .cin(undriven_3), .cout(adder_3_cout));
  assign bit_extender_1_out = {{7{1'b0}}, or_3_out};  // Bit_Extender bit_extender_1
  assign bit_extender_1_out = {{7{1'b0}}, or_3_out};  // Bit_Extender bit_extender_2
  assign bit_extender_3_out = {{7{1'b0}}, comparator_3_gt};  // Bit_Extender bit_extender_3
  assign bit_extender_3_out = {{7{1'b0}}, comparator_3_gt};  // Bit_Extender bit_extender_4
  assign bit_extender_5_out = {{7{1'b0}}, comparator_3_eq};  // Bit_Extender bit_extender_5
  assign bit_extender_5_out = {{7{1'b0}}, comparator_3_eq};  // Bit_Extender bit_extender_6
  assign bit_extender_7_out = {{7{1'b0}}, comparator_3_lt};  // Bit_Extender bit_extender_7
  assign bit_extender_7_out = {{7{1'b0}}, comparator_3_lt};  // Bit_Extender bit_extender_8
  Multiplexer #(.width(8), .enable("false")) multiplexer_1 (
    .in0(adder_3_out), .in1(New_PC_value), .out(multiplexer_1_out), .sel(comparator_1_gt));
  Multiplexer #(.width(8), .enable("false")) multiplexer_2 (
    .in0(adder_3_out), .in1(New_PC_value), .out(multiplexer_1_out), .sel(comparator_1_gt));
  Multiplexer #(.width(8), .enable("false")) multiplexer_3 (
    .in0(adder_3_out), .in1(New_PC_value), .out(multiplexer_3_out), .sel(comparator_1_eq));
  Multiplexer #(.width(8), .enable("false")) multiplexer_4 (
    .in0(adder_3_out), .in1(New_PC_value), .out(multiplexer_3_out), .sel(comparator_1_eq));
  Multiplexer #(.width(8), .enable("false")) multiplexer_5 (
    .in0(adder_3_out), .in1(New_PC_value), .out(multiplexer_5_out), .sel(comparator_1_lt));
  Multiplexer #(.width(8), .enable("false")) multiplexer_6 (
    .in0(adder_3_out), .in1(New_PC_value), .out(multiplexer_5_out), .sel(comparator_1_lt));
  Multiplexer #(.select(4), .width(8), .enable("false")) multiplexer_7 (
    .in0(adder_1_out), .in1(subtractor_1_out), .in2(negator_1_out), .in3(Reg_A), .in4(and_1_out),
    .in5(or_1_out), .in6(bit_extender_1_out), .in7(bit_extender_3_out), .in8(bit_extender_5_out),
    .in9(bit_extender_7_out), .in10(multiplexer_1_out), .in11(multiplexer_3_out), .in12(multiplexer_5_out),
    .in13(undriven_4), .in14(undriven_5), .in15(undriven_6), .out(ALU_output), .sel(in_2));
  Multiplexer #(.select(4), .width(8), .enable("false")) multiplexer_8 (
    .in0(adder_1_out), .in1(subtractor_1_out), .in2(negator_1_out), .in3(Reg_A), .in4(and_1_out),
    .in5(or_1_out), .in6(bit_extender_1_out), .in7(bit_extender_3_out), .in8(bit_extender_5_out),
    .in9(bit_extender_7_out), .in10(multiplexer_1_out), .in11(multiplexer_3_out), .in12(multiplexer_5_out),
    .in13(undriven_4), .in14(undriven_5), .in15(undriven_6), .out(ALU_output), .sel(in_2));

  assign ALU_output_2 = ALU_output;
  assign in_3 = in_2;
  assign in_5 = in_4;
  assign in_9 = in_8;
  assign New_PC_value_2 = New_PC_value;

  // Notes on the sheet:
  //   Reg A
  //   Reg B
  //   Reg B
  //   0 Plus
  //   0 Plus
  //   1 Minus
  //   1 Minus
  //   2 Negate
  //   2 Negate
  //   3 Pass through
  //   3 Pass through
  //   4 And
  //   4 And
  //   5 Or
  //   5 Or
  //   6 Bool Invert
  //   6 Bool Invert
  //   7 Greater Than
  //   7 Greater Than
  //   8 Equal
  //   8 Equal
  //   9 Less Than
  //   9 Less Than
  //   10 Jump if >
  //   10 Jump if >
  //   11 Jump if =
  //   11 Jump if =
  //   12 Jump if <
  //   12 Jump if <
  //   Current PC value
  //   Current PC value
  //   Operation Selector
  //   Operation Selector
endmodule
