// Logisim project networkBridge.circ as structural Verilog: 3 circuits, main circuit main
module main (
  input  write,
  input  read,
  input  [7:0] write_data,
  output [1:0] out_4,
  output [1:0] out_5,
  output Writable,
  output Readable,
  output [1:0] out_8,
  output [7:0] readdata
);

  wire and_1_out, and_2_out, comparator_1_eq, comparator_2_eq, decoder_1_out0, decoder_1_out1,
       decoder_1_out2, decoder_1_out3;
  wire [1:0] adder_1_out;
  wire [7:0] register_1_q, register_2_q, register_3_q, register_4_q;

  and and_1 (and_1_out, write, Writable);
  smallCounter smallcounter_1 (.out_3(out_4), .in_2(and_1_out));  // open: in_1
  and and_2 (and_2_out, read, Readable);
  smallCounter smallcounter_2 (.out_3(out_5), .in_2(and_2_out));  // open: in_1
  Adder #(.width(2)) adder_1 (.a(out_4), .b(2'b01), .out(adder_1_out));  // open: cin, cout
  Comparator #(.width(2)) comparator_1 (.a(out_4), .b(out_5), .eq(comparator_1_eq));  // open: gt, lt
  Comparator #(.width(2)) comparator_2 (.a(out_5), .b(adder_1_out), .eq(comparator_2_eq));  // open: gt, lt
  not not_1 (Readable, comparator_1_eq);
  not not_2 (Writable, comparator_2_eq);
  Decoder #(.select(2), .enable("false")) decoder_1 (
    .out0(decoder_1_out0), .out1(decoder_1_out1), .out2(decoder_1_out2), .out3(decoder_1_out3), .sel(out_4));
  Register register_1 (.D(write_data), .en(decoder_1_out0), .clk(and_1_out), .Q(register_1_q));  // open: clr
  Register register_2 (.D(write_data), .en(decoder_1_out1), .clk(and_1_out), .Q(register_2_q));  // open: clr
  Register register_3 (.D(write_data), .en(decoder_1_out2), .clk(and_1_out), .Q(register_3_q));  // open: clr
  Register register_4 (.D(write_data), .en(decoder_1_out3), .clk(and_1_out), .Q(register_4_q));  // open: clr
  Multiplexer #(.select(2), .width(8), .enable("false")) multiplexer_1 (
    .in0(register_1_q), .in1(register_2_q), .in2(register_3_q), .in3(register_4_q), .out(readdata),
    .sel(out_5));

  assign out_8 = out_5;

  // Notes on the sheet:
  //   This is a buffer that can be read from and written to using different clock signals.
  //   This lets one computer write to it, and another read from it, when they're on different clocks.
  //   00
  //   01
  //   10
  //   11
endmodule

module smallCounter (
  input  in_1,
  input  in_2,
  output [1:0] out_3
);

  Counter #(.width(2), .max('h3)) counter_1 (.clr(in_1), .clk(in_2), .Q(out_3));  // open: load, up, count, D, carry

  // Notes on the sheet:
  //   This counter is too big. Make it into a module.
endmodule

module test (
  input  [1:0] in_1,
  input  [1:0] in_2,
  output [1:0] out_3,
  output [7:0] out_4,
  output [1:0] out_5
);

  wire and_1_out, and_2_out, button_1_out, button_2_out, button_3_out, button_4_out, main_1_readable,
       main_1_writable;
  wire [7:0] counter_1_q, counter_2_q, main_1_readdata;

  Button button_1 (.out(button_1_out));
  Button button_2 (.out(button_2_out));
  RAM #(.databus("bibus")) ram_1 (
    .addr(counter_1_q), .we(1'b0), .oe(1'b1), .clk(and_1_out), .dout(out_4));  // open: din
  Counter counter_1 (.clr(button_1_out), .load(1'b0), .clk(and_1_out), .Q(counter_1_q));  // open: up, count, D, carry
  and and_1 (and_1_out, main_1_writable, button_2_out);
  // BCD_to_7_Segment_decoder bcd_to_7_segment_decoder_1: pin names not known; wires that end beside it: {in_1, out_3}
  _7_Segment_Display u_7_segment_display_1 ();  // open: g, f, a, b, e, d, c, dp
  main main_1 (
    .Readable(main_1_readable), .Writable(main_1_writable), .out_5(out_5), .out_4(out_3), .write_data(out_4),
    .read(and_2_out), .write(and_1_out), .readdata(main_1_readdata));  // open: out_8
  _7_Segment_Display u_7_segment_display_2 ();  // open: g, f, a, b, e, d, c, dp
  // BCD_to_7_Segment_decoder bcd_to_7_segment_decoder_2: pin names not known; wires that end beside it: {in_2, out_5}
  Button button_3 (.out(button_3_out));
  and and_2 (and_2_out, main_1_readable, button_3_out);
  RAM #(.databus("bibus")) ram_2 (
    .addr(counter_2_q), .we(1'b1), .clk(and_2_out), .din(main_1_readdata));  // open: oe, dout
  Counter counter_2 (.clr(button_4_out), .clk(and_2_out), .Q(counter_2_q));  // open: load, up, count, D, carry
  Button button_4 (.out(button_4_out));

  // Notes on the sheet:
  //   Write
  //   Test that the bridge works
  //   Highlighted one is the one waiting to be written
  //   Read
  //   Highlighted one is the one most recently read
endmodule
